# Fritzing sketch schema (saved by Fritzing 0.8.5b)
breadboards: 1

parts:
  J1 = Basic Servo
  J2 = Basic Servo
  J3 = Basic Servo
  J4 = Basic Servo
  J5 = Basic Servo
  J6 = Basic Servo
  Composants1 = Arduino Uno (Rev3)
  Composants2 = SRF05 Ultrasonic Rangefinder

nets:
  GND: J1.gnd, J2.gnd, J3.gnd, J4.gnd, J5.gnd, J6.gnd, Composants1.GND, Composants2.GND
  VCC: J1.vcc, J2.vcc, J3.vcc, J4.vcc, J5.vcc, J6.vcc, Composants1.VIN, Composants2.VCC
  N1: J1.pulse, Composants1.D7
  N2: J2.pulse, Composants1.D6_PWM
  N3: J3.pulse, Composants1.D5_PWM
  N4: J4.pulse, Composants1.D4
  N5: J5.pulse, Composants1.D3_PWM
  N6: J6.pulse, Composants1.D2
  N7: Composants1.D11_PWM/MOSI, Composants2.Echo
  N8: Composants1.D13/SCK, Composants2.Trig
